# Fritzing sketch fritzing (saved by Fritzing 0.9.3b)
breadboards: 1

parts:
  Componente1 = Arduino Mega 2560 (Rev3)
  VCC1 = Battery
  VCC2 = Battery
  J1 = Basic Servo
  J2 = Basic Servo
  J3 = Basic Servo
  J4 = Basic Servo
  J5 = Basic Servo
  J6 = Basic Servo
  J7 = Basic Servo
  J8 = Basic Servo
  J9 = Basic Servo
  J10 = Basic Servo
  J11 = Basic Servo
  J12 = Basic Servo
  J13 = Basic Servo
  J14 = Basic Servo
  Raspberry_Pi_1 = Raspberry Pi 3 [part_number=RPI-3-V1.2]  # not connected
  VCC3 = Battery
  VCC4 = Battery
  hc-sr1 = hc-sr04  # not connected
  hc-sr2 = hc-sr04  # not connected
  hc-sr3 = hc-sr04  # not connected

nets:
  GND: Componente1.GND, VCC2.-, J1.gnd, J2.gnd, J3.gnd, J4.gnd, J5.gnd, J6.gnd, J7.gnd, J8.gnd, J9.gnd, J10.gnd, J11.gnd, J12.gnd, J13.gnd, J14.gnd, VCC3.-
  N1: Componente1.D22, J3.pulse
  N2: Componente1.D24, J2.pulse
  N3: Componente1.D26, J1.pulse
  N4: Componente1.D28, J9.pulse
  N5: Componente1.D30, J8.pulse
  N6: Componente1.D32, J7.pulse
  N7: Componente1.D34, J6.pulse
  N8: Componente1.D36, J5.pulse
  N9: Componente1.D38, J4.pulse
  N10: Componente1.D40, J12.pulse
  N11: Componente1.D42, J11.pulse
  N12: Componente1.D44, J10.pulse
  N13: Componente1.D48, J13.pulse
  VCC: VCC1.+, J1.vcc, J2.vcc, J3.vcc, J4.vcc, J5.vcc, J6.vcc, J7.vcc, J8.vcc, J9.vcc, J10.vcc, J11.vcc, J12.vcc, J13.vcc, J14.vcc, VCC4.+

notes:
  usb
  Power Bank
